# Fritzing sketch Luci2 (saved by Fritzing 0.9.3b)
circuit board: 4.83042cm x 8.5598cm
breadboards: 1

parts:
  R2 = Resistor [tolerance=±5% resistance=10k package="0805 [SMD]"]
  1µF = Ceramic Capacitor [capacitance=1µF package="0805 [SMD, multilayer]"]
  AS7262 = LGA-20
  BT = LED - 3mm [color="Blue (505nm)" package="3 mm [THT]"]
  0_1µF = Ceramic Capacitor [capacitance=100nF package="0805 [SMD, multilayer]"]
  10µF = Ceramic Capacitor [capacitance=10µF package="0805 [SMD, multilayer]"]
  R6 = Resistor [tolerance=±5% resistance=10k package="0805 [SMD]"]
  TX = male pin header, 3 pins [form="♂ (male)"]
  ESP32 = ESP32
  R1 = Resistor [tolerance=±5% resistance=10k package="0805 [SMD]"]
  IC2 = AT25SF041
  10µF_2 = Ceramic Capacitor [capacitance=10µF package="1206 [SMD, multilayer]"]
  R3 = Resistor [tolerance=±5% resistance=10k package="0805 [SMD]"]
  R7 = Resistor [tolerance=±5% resistance=10k package="1206 [SMD]"]
  R6_2 = Resistor [tolerance=±5% resistance=10k package="0805 [SMD]"]
  10µF_3 = Ceramic Capacitor [capacitance=10µF package="0805 [SMD, multilayer]"]
  IC1 = TC4056A
  Rdy = LED - 3mm [color="Red (633nm)" package="3 mm [THT]"]
  + = Header 2 [package=jst-2-pth]
  R5 = Resistor [tolerance=±5% resistance=10k package="0805 [SMD]"]
  R7_2 = Resistor [tolerance=±5% resistance=10k package="0805 [SMD]"]
  10µF_4 = Ceramic Capacitor [capacitance=10µF package="1206 [SMD, multilayer]"]
  Pad1 = Pad [width=3.5 height=1.75 connect=center]  # not connected
  Chrg = LED - 3mm [color="Green (560nm)" package="3 mm [THT]"]
  1117 = Voltage Regulator AMS1117 [package=sot223]
  Pad2 = Pad [width=2.2666083114213773 height=4.5638463084351883 connect=center]
  Pad3 = Pad [width=2.2666083114213773 height=4.5638463084351883 connect=center]  # not connected

nets:
  3.3V: R2.Pin_0, 1µF.1, AS7262.VDD2, AS7262.VDD1, BT.anode, 0_1µF.1, 10µF.1, ESP32.3v3, ESP32.EN, R1.Pin_0, IC2.WP, IC2.HOLD, IC2.VCC, R3.Pin_1, R6_2.Pin_0, 10µF_3.0, 1117.VOut
  SDA1: R2.Pin_1, AS7262.TX/SDA_S, ESP32.IO21
  N1: AS7262.RESN, R6_2.Pin_1
  N2: AS7262.SCK, IC2.SCK
  N3: AS7262.MOSI, IC2.SI
  N4: AS7262.MISO, IC2.SO
  N5: AS7262.CSN_EE, IC2.CS
  N6: AS7262.I2C_ENB, R3.Pin_0
  SC1: AS7262.RX/SCL_S, ESP32.IO22, R1.Pin_1
  N7: BT.cathode, ESP32.IO12
  N8: 0_1µF.0, 10µF.0
  N9: R6.Pin_0, IC1.STDBY
  N10: R6.Pin_1, Chrg.cathode
  N11: TX.pin1, ESP32.TX
  N12: TX.pin2, ESP32.RX
  N13: 10µF_2.1, 1117.IN
  VCC: R7.Pin_0, IC1.VCC, IC1.CE, 10µF_4.1
  N14: R7.Pin_1, Rdy.anode, Chrg.anode, Pad2.pad
  N15: IC1.PROG, R7_2.Pin_0
  GND: IC1.BAT, +.2
  N16: IC1.CHRG, R5.Pin_0
  N17: Rdy.cathode, R5.Pin_1
  Switch: +.1

notes:
  Copyright 2017-2018
  Object Syndicate LLC
