# Fritzing sketch Luci_revised (saved by Fritzing 0.9.3b)
circuit board: 5.65cm x 8.80001cm
breadboards: 1

parts:
  ESP32 = ESP32
  1117 = Voltage Regulator AMS1117 [package=sot223]
  AS7263 = LGA-20
  IC2 = AT25SF041
  R4 = Resistor [tolerance=±5% resistance=10k package="0805 [SMD]"]
  R6 = Resistor [tolerance=±5% resistance=10k package="0805 [SMD]"]
  R3 = Resistor [tolerance=±5% resistance=10k package="0805 [SMD]"]
  R5 = Resistor [tolerance=±5% resistance=10k package="0805 [SMD]"]
  1µF = Ceramic Capacitor [capacitance=1µF package="0805 [SMD, multilayer]"]
  1µF_2 = Ceramic Capacitor [capacitance=1µF package="0805 [SMD, multilayer]"]
  0_1µF = Ceramic Capacitor [capacitance=100nF package="0805 [SMD, multilayer]"]
  10µF = Ceramic Capacitor [capacitance=10µF package="0805 [SMD, multilayer]"]
  0_1µF_2 = Ceramic Capacitor [capacitance=100nF package="0805 [SMD, multilayer]"]
  AS7262 = LGA-20
  IC3 = AT25SF041
  10µF_2 = Ceramic Capacitor [capacitance=10µF package="0805 [SMD, multilayer]"]
  IC1 = PCA9540B [chip_label=?]
  10µF_3 = Ceramic Capacitor [capacitance=10µF package="0805 [SMD, multilayer]"]
  R1 = Resistor [tolerance=±5% resistance=10k package="0805 [SMD]"]
  R2 = Resistor [tolerance=±5% resistance=10k package="0805 [SMD]"]
  BT = LED - 3mm [color="Blue (505nm)" package="3 mm [THT]"]
  C8 = Ceramic Capacitor [capacitance=10µF package="0805 [SMD, multilayer]"]  # not connected
  IC6 = TC4056A
  Chrg = LED - 3mm [color="Green (560nm)" package="3 mm [THT]"]
  Rdy = LED - 3mm [color="Red (633nm)" package="3 mm [THT]"]
  R7 = Resistor [tolerance=±5% resistance=10k package="1206 [SMD]"]
  10µF_4 = Ceramic Capacitor [capacitance=10µF package="1206 [SMD, multilayer]"]
  10µF_5 = Ceramic Capacitor [capacitance=10µF package="1206 [SMD, multilayer]"]
  R9 = Resistor [tolerance=±5% resistance=10k package="0805 [SMD]"]
  R10 = Resistor [tolerance=±5% resistance=10k package="0805 [SMD]"]
  R8 = Resistor [tolerance=±5% resistance=10k package="0805 [SMD]"]
  Pad1 = Pad [width=3.5 height=1.75 connect=center]  # not connected
  TX = male pin header, 3 pins [form="♂ (male)"]
  + = Header 2 [package=jst-2-pth]

nets:
  3.3V: ESP32.3v3, ESP32.EN, 1117.VOut, AS7263.VDD2, AS7263.VDD1, IC2.WP, IC2.HOLD, IC2.VCC, R4.Pin_1, R6.Pin_0, R3.Pin_1, R5.Pin_0, 1µF.1, 1µF_2.1, 0_1µF.0, 10µF.0, 0_1µF_2.0, AS7262.VDD2, AS7262.VDD1, IC3.WP, IC3.HOLD, IC3.VCC, 10µF_2.0, IC1.Vdd, 10µF_3.0, BT.anode
  N1: ESP32.IO12, BT.cathode
  N2: ESP32.IO21, IC1.SDA, R2.Pin_1
  N3: ESP32.RX, TX.pin2
  N4: ESP32.TX, TX.pin1
  N5: ESP32.IO22, IC1.SCL, R1.Pin_1
  N6: 1117.IN, 10µF_5.1
  N7: AS7263.RESN, R5.Pin_1
  N8: AS7263.SCK, IC2.SCK
  N9: AS7263.MOSI, IC2.SI
  N10: AS7263.MISO, IC2.SO
  N11: AS7263.CSN_EE, IC2.CS
  N12: AS7263.I2C_ENB, R3.Pin_0
  N13: AS7263.RX/SCL_S, IC1.SC0
  N14: AS7263.TX/SDA_S, IC1.SD0
  N15: R4.Pin_0, AS7262.I2C_ENB
  N16: R6.Pin_1, AS7262.RESN
  N17: 0_1µF.1, 10µF_2.1
  N18: 10µF.1, 0_1µF_2.1
  N19: AS7262.SCK, IC3.SCK
  N20: AS7262.MOSI, IC3.SI
  N21: AS7262.MISO, IC3.SO
  N22: AS7262.CSN_EE, IC3.CS
  SC1: AS7262.RX/SCL_S, IC1.SC1
  SDA1: AS7262.TX/SDA_S, IC1.SD1
  N23: IC6.PROG, R8.Pin_0
  VCC: IC6.VCC, IC6.CE, R7.Pin_0, 10µF_4.1
  GND: IC6.BAT, +.2
  N24: IC6.STDBY, R9.Pin_0
  N25: IC6.CHRG, R10.Pin_0
  N26: Chrg.cathode, R9.Pin_1
  N27: Chrg.anode, Rdy.anode, R7.Pin_1
  N28: Rdy.cathode, R10.Pin_1
  Switch: +.1

notes:
  Copyright 2017-2018
  Object Syndicate LLC
